# Fritzing sketch rpi-powerbtn (saved by Fritzing 0.7.7b)
breadboards: 1

parts:
  5V = Power plug
  5V_(ALT) = Screw terminal - 2 pins [package=THT]
  3V3 = LD33 Low-Dropout Voltage Regulator
  AVR = attiny85 [package=dip]
  Pi = shrouded pin header, 26 pins [form="♂ (shrouded male)"]
  FETP = Basic FET P-Channel [part_number=NT2955G package="TO220 [THT]"]
  R1 = Resistor [tolerance=±5% resistance=10k package=THT]
  S1 = Pushbutton [package=THT]
  R2 = Resistor [tolerance=±5% resistance=10k package=THT]
  LED1 = LED - 5mm [color="Red (633nm)" package="5 mm [THT]"]
  R3 = Resistor [tolerance=±5% resistance=10k package=THT]
  R4 = Resistor [tolerance=±5% resistance=220 package=THT]
  C2 = Electrolytic Capacitor [capacitance=10µF package="100 mil [THT, electrolytic]"]
  C1 = Electrolytic Capacitor [capacitance=100µF package="100 mil [THT, electrolytic]"]
  C3 = Ceramic Capacitor [capacitance=1µF package="100 mil [THT, multilayer]"]
  C4 = Ceramic Capacitor [capacitance=100nF package="100 mil [THT, multilayer]"]
  S2 = Pushbutton [package=THT]
  R5 = Resistor [tolerance=±5% resistance=10k package=THT]
  ICSP = shrouded pin header, 6 pins [form="♂ (shrouded male)"]

nets:
  GND: 5V.GND, 5V_(ALT).pin2, 3V3.GND, AVR.Pin_4, Pi.pin24, S1.leg0, R2.Pin_0, R3.Pin_0, R4.Pin_0, C2.-, C1.-, C3.0, C4.0, R5.Pin_0, ICSP.pin4
  VCC: 5V.VCC, 5V_(ALT).pin1, 3V3.Vin, FETP.source
  N1: 3V3.Vout, AVR.Pin_8, R1.Pin_0, C2.+, C1.+, C3.1, C4.1, S2.leg0, ICSP.pin6
  N2: AVR.Pin_1, R1.Pin_1, S1.leg1, ICSP.pin3
  N3: AVR.Pin_2, Pi.pin19, R2.Pin_1
  N4: AVR.Pin_3, Pi.pin18
  N5: AVR.Pin_5, FETP.gate, R3.Pin_1, ICSP.pin5
  N6: AVR.Pin_6, LED1.anode, ICSP.pin1
  N7: AVR.Pin_7, S2.leg1, R5.Pin_1, ICSP.pin2
  N8: Pi.pin26, FETP.drain
  N9: LED1.cathode, R4.Pin_1
